// Digital circuit GetRegisters.dig as structural Verilog
module GetRegisters (
  input  [31:0] R1,
  input  [31:0] R2,
  input  [31:0] R3,
  input  SetD,
  input  [31:0] Data,
  input  [31:0] RD
);

  ShiftLeft shiftleft_1 (.A(32'h1), .B(R1));  // open: Out
  ShiftLeft shiftleft_2 (.A(32'h1), .B(R2));  // open: Out
  ShiftLeft shiftleft_3 (.A(32'h1), .B(R3));  // open: Out
  ShiftLeft shiftleft_4 (.A(32'h1), .B(RD));  // open: Out
endmodule
