// Digital circuit RegisterBit.dig as structural Verilog
module RegisterBit (
  input  Data,
  input  Str,
  output Out
);

  wire and_1_out;

  ConBit conbit_1 (.A(and_1_out), .B(Data), .Condition(Str), .Out(Out));
  and and_1 (and_1_out, Out, Out);
endmodule
