// Digital circuit Placeholder.dig as structural Verilog
module Placeholder (
);

  Register register_1 ();  // open: Data, Str, Out
  AddInt addint_1 ();  // open: A, B, Sum, Overflow
  SubInt subint_1 ();  // open: A, B, Sub, Underflow
  ShiftLeft shiftleft_1 ();  // open: A, B, Out
  ShiftRight shiftright_1 ();  // open: A, B, Out
endmodule
